// Logisim project control-logic.circ as structural Verilog: 1 circuit, main circuit control_logic
module control_logic (
  input  [31:0] Instruction,
  input  BrEq,
  input  BrLt,
  output PCSel,
  output RegWEn,
  output [2:0] ImmSel,
  output BrUn,
  output ASel,
  output BSel,
  output [3:0] ALUSel,
  output MemRW,
  output [1:0] WBSel
);

  wire and_33_out, and_34_out, and_35_out, and_36_out, and_37_out, and_38_out, and_39_out, comparator_1_eq,
       comparator_2_eq, comparator_3_eq, comparator_4_eq, comparator_5_eq, comparator_6_eq, comparator_7_eq,
       comparator_8_eq, comparator_9_eq, comparator_10_eq, comparator_11_eq, comparator_12_eq,
       comparator_13_eq, comparator_14_eq, comparator_15_eq, comparator_16_eq, comparator_17_eq,
       comparator_18_eq, comparator_19_eq, comparator_20_eq, comparator_21_eq, comparator_22_eq,
       comparator_23_eq, comparator_24_eq, comparator_25_eq, comparator_26_eq, comparator_27_eq,
       comparator_28_eq, comparator_29_eq, comparator_30_eq, comparator_31_eq, comparator_32_eq,
       comparator_33_eq, comparator_34_eq, comparator_35_eq, comparator_36_eq, comparator_37_eq,
       comparator_38_eq, comparator_39_eq, comparator_40_eq, comparator_41_eq, comparator_42_eq,
       comparator_43_eq, comparator_44_eq, comparator_45_eq, comparator_46_eq, comparator_47_eq,
       comparator_48_eq, comparator_49_eq, comparator_50_eq, comparator_51_eq, comparator_52_eq,
       comparator_53_eq, comparator_54_eq, comparator_55_eq, comparator_56_eq, comparator_57_eq,
       comparator_58_eq, comparator_59_eq, comparator_60_eq, comparator_61_eq, comparator_62_eq,
       comparator_63_eq, comparator_64_eq, comparator_65_eq, comparator_66_eq, comparator_67_eq,
       comparator_68_eq, comparator_69_eq, comparator_70_eq, comparator_71_eq, comparator_72_eq,
       comparator_73_eq, comparator_74_eq, comparator_75_eq, comparator_76_eq, is_add, is_addi, is_and,
       is_andi, is_beq, is_bge, is_bgeu, is_blt, is_bltu, is_bne, is_lb, is_lh, is_lw, is_mul, is_mulh,
       is_mulhu, is_or, is_ori, is_sb, is_sh, is_sll, is_slli, is_slt, is_slti, is_sra, is_srai, is_srl,
       is_srli, is_sub, is_sw, is_xor, is_xori, not_1_out, not_2_out, not_3_out, or_1_out, or_2_out;
  wire [5:0] input_ROM;
  wire [15:14] rom_1_data;

  Comparator #(.width(5)) comparator_1 (.a(Instruction[6:2]), .b(5'b00100), .eq(comparator_1_eq));  // open: gt, lt
  Comparator #(.width(3)) comparator_2 (.a(Instruction[14:12]), .b(3'b000), .eq(comparator_2_eq));  // open: gt, lt
  Comparator #(.width(5)) comparator_3 (.a(Instruction[6:2]), .b(5'b00100), .eq(comparator_3_eq));  // open: gt, lt
  Comparator #(.width(3)) comparator_4 (.a(Instruction[14:12]), .b(3'b111), .eq(comparator_4_eq));  // open: gt, lt
  Comparator #(.width(5)) comparator_5 (.a(Instruction[6:2]), .b(5'b00100), .eq(comparator_5_eq));  // open: gt, lt
  Comparator #(.width(3)) comparator_6 (.a(Instruction[14:12]), .b(3'b110), .eq(comparator_6_eq));  // open: gt, lt
  Comparator #(.width(5)) comparator_7 (.a(Instruction[6:2]), .b(5'b00100), .eq(comparator_7_eq));  // open: gt, lt
  Comparator #(.width(3)) comparator_8 (.a(Instruction[14:12]), .b(3'b100), .eq(comparator_8_eq));  // open: gt, lt
  Comparator #(.width(5)) comparator_9 (.a(Instruction[6:2]), .b(5'b00100), .eq(comparator_9_eq));  // open: gt, lt
  Comparator #(.width(3)) comparator_10 (.a(Instruction[14:12]), .b(3'b001), .eq(comparator_10_eq));  // open: gt, lt
  Comparator #(.width(1)) comparator_11 (.a(Instruction[30]), .b(1'b0), .eq(comparator_11_eq));  // open: gt, lt
  Comparator #(.width(5)) comparator_12 (.a(Instruction[6:2]), .b(5'b00100), .eq(comparator_12_eq));  // open: gt, lt
  Comparator #(.width(3)) comparator_13 (.a(Instruction[14:12]), .b(3'b101), .eq(comparator_13_eq));  // open: gt, lt
  Comparator #(.width(1)) comparator_14 (.a(Instruction[30]), .b(1'b0), .eq(comparator_14_eq));  // open: gt, lt
  Comparator #(.width(5)) comparator_15 (.a(Instruction[6:2]), .b(5'b00100), .eq(comparator_15_eq));  // open: gt, lt
  Comparator #(.width(3)) comparator_16 (.a(Instruction[14:12]), .b(3'b101), .eq(comparator_16_eq));  // open: gt, lt
  Comparator #(.width(1)) comparator_17 (.a(Instruction[30]), .b(1'b1), .eq(comparator_17_eq));  // open: gt, lt
  Comparator #(.width(5)) comparator_18 (.a(Instruction[6:2]), .b(5'b00100), .eq(comparator_18_eq));  // open: gt, lt
  Comparator #(.width(3)) comparator_19 (.a(Instruction[14:12]), .b(3'b010), .eq(comparator_19_eq));  // open: gt, lt
  Comparator #(.width(5)) comparator_20 (.a(Instruction[6:2]), .b(5'b01100), .eq(comparator_20_eq));  // open: gt, lt
  Comparator #(.width(3)) comparator_21 (.a(Instruction[14:12]), .b(3'b000), .eq(comparator_21_eq));  // open: gt, lt
  Comparator #(.width(1)) comparator_22 (.a(Instruction[30]), .b(1'b0), .eq(comparator_22_eq));  // open: gt, lt
  Comparator #(.width(5)) comparator_23 (.a(Instruction[6:2]), .b(5'b01100), .eq(comparator_23_eq));  // open: gt, lt
  Comparator #(.width(3)) comparator_24 (.a(Instruction[14:12]), .b(3'b000), .eq(comparator_24_eq));  // open: gt, lt
  Comparator #(.width(1)) comparator_25 (.a(Instruction[30]), .b(1'b1), .eq(comparator_25_eq));  // open: gt, lt
  Comparator #(.width(5)) comparator_26 (.a(Instruction[6:2]), .b(5'b01100), .eq(comparator_26_eq));  // open: gt, lt
  Comparator #(.width(3)) comparator_27 (.a(Instruction[14:12]), .b(3'b111), .eq(comparator_27_eq));  // open: gt, lt
  Comparator #(.width(1)) comparator_28 (.a(Instruction[30]), .b(1'b0), .eq(comparator_28_eq));  // open: gt, lt
  Comparator #(.width(5)) comparator_29 (.a(Instruction[6:2]), .b(5'b01100), .eq(comparator_29_eq));  // open: gt, lt
  Comparator #(.width(3)) comparator_30 (.a(Instruction[14:12]), .b(3'b110), .eq(comparator_30_eq));  // open: gt, lt
  Comparator #(.width(1)) comparator_31 (.a(Instruction[30]), .b(1'b0), .eq(comparator_31_eq));  // open: gt, lt
  Comparator #(.width(5)) comparator_32 (.a(Instruction[6:2]), .b(5'b01100), .eq(comparator_32_eq));  // open: gt, lt
  Comparator #(.width(3)) comparator_33 (.a(Instruction[14:12]), .b(3'b100), .eq(comparator_33_eq));  // open: gt, lt
  Comparator #(.width(1)) comparator_34 (.a(Instruction[30]), .b(1'b0), .eq(comparator_34_eq));  // open: gt, lt
  Comparator #(.width(5)) comparator_35 (.a(Instruction[6:2]), .b(5'b01100), .eq(comparator_35_eq));  // open: gt, lt
  Comparator #(.width(3)) comparator_36 (.a(Instruction[14:12]), .b(3'b001), .eq(comparator_36_eq));  // open: gt, lt
  Comparator #(.width(1)) comparator_37 (.a(Instruction[30]), .b(1'b0), .eq(comparator_37_eq));  // open: gt, lt
  Comparator #(.width(5)) comparator_38 (.a(Instruction[6:2]), .b(5'b01100), .eq(comparator_38_eq));  // open: gt, lt
  Comparator #(.width(3)) comparator_39 (.a(Instruction[14:12]), .b(3'b101), .eq(comparator_39_eq));  // open: gt, lt
  Comparator #(.width(1)) comparator_40 (.a(Instruction[30]), .b(1'b0), .eq(comparator_40_eq));  // open: gt, lt
  Comparator #(.width(5)) comparator_41 (.a(Instruction[6:2]), .b(5'b01100), .eq(comparator_41_eq));  // open: gt, lt
  Comparator #(.width(3)) comparator_42 (.a(Instruction[14:12]), .b(3'b101), .eq(comparator_42_eq));  // open: gt, lt
  Comparator #(.width(1)) comparator_43 (.a(Instruction[30]), .b(1'b1), .eq(comparator_43_eq));  // open: gt, lt
  Comparator #(.width(5)) comparator_44 (.a(Instruction[6:2]), .b(5'b01100), .eq(comparator_44_eq));  // open: gt, lt
  Comparator #(.width(3)) comparator_45 (.a(Instruction[14:12]), .b(3'b010), .eq(comparator_45_eq));  // open: gt, lt
  Comparator #(.width(1)) comparator_46 (.a(Instruction[30]), .b(1'b0), .eq(comparator_46_eq));  // open: gt, lt
  Comparator #(.width(5)) comparator_47 (.a(Instruction[6:2]), .b(5'b01100), .eq(comparator_47_eq));  // open: gt, lt
  Comparator #(.width(3)) comparator_48 (.a(Instruction[14:12]), .b(3'b000), .eq(comparator_48_eq));  // open: gt, lt
  Comparator #(.width(1)) comparator_49 (.a(Instruction[25]), .b(1'b1), .eq(comparator_49_eq));  // open: gt, lt
  Comparator #(.width(3)) comparator_50 (.a(Instruction[14:12]), .b(3'b001), .eq(comparator_50_eq));  // open: gt, lt
  Comparator #(.width(3)) comparator_51 (.a(Instruction[14:12]), .b(3'b011), .eq(comparator_51_eq));  // open: gt, lt
  Comparator #(.width(5)) comparator_52 (.a(Instruction[6:2]), .b(5'b11000), .eq(comparator_52_eq));  // open: gt, lt
  Comparator #(.width(3)) comparator_53 (.a(Instruction[14:12]), .b(3'b000), .eq(comparator_53_eq));  // open: gt, lt
  Comparator #(.width(3)) comparator_54 (.a(Instruction[14:12]), .b(3'b101), .eq(comparator_54_eq));  // open: gt, lt
  Comparator #(.width(3)) comparator_55 (.a(Instruction[14:12]), .b(3'b111), .eq(comparator_55_eq));  // open: gt, lt
  Comparator #(.width(3)) comparator_56 (.a(Instruction[14:12]), .b(3'b100), .eq(comparator_56_eq));  // open: gt, lt
  Comparator #(.width(3)) comparator_57 (.a(Instruction[14:12]), .b(3'b110), .eq(comparator_57_eq));  // open: gt, lt
  Comparator #(.width(3)) comparator_58 (.a(Instruction[14:12]), .b(3'b001), .eq(comparator_58_eq));  // open: gt, lt
  Comparator #(.width(5)) comparator_59 (.a(Instruction[6:2]), .b({5{1'b0}}), .eq(comparator_59_eq));  // open: gt, lt
  Comparator #(.width(3)) comparator_60 (.a(Instruction[14:12]), .b(3'b000), .eq(comparator_60_eq));  // open: gt, lt
  Comparator #(.width(3)) comparator_61 (.a(Instruction[14:12]), .b(3'b001), .eq(comparator_61_eq));  // open: gt, lt
  Comparator #(.width(3)) comparator_62 (.a(Instruction[14:12]), .b(3'b010), .eq(comparator_62_eq));  // open: gt, lt
  Comparator #(.width(5)) comparator_63 (.a(Instruction[6:2]), .b(5'b01000), .eq(comparator_63_eq));  // open: gt, lt
  Comparator #(.width(3)) comparator_64 (.a(Instruction[14:12]), .b(3'b000), .eq(comparator_64_eq));  // open: gt, lt
  Comparator #(.width(3)) comparator_65 (.a(Instruction[14:12]), .b(3'b001), .eq(comparator_65_eq));  // open: gt, lt
  Comparator #(.width(3)) comparator_66 (.a(Instruction[14:12]), .b(3'b111), .eq(comparator_66_eq));  // open: gt, lt
  and and_1 (is_addi, comparator_1_eq, comparator_2_eq);
  and and_2 (is_andi, comparator_3_eq, comparator_4_eq);
  and and_3 (is_ori, comparator_5_eq, comparator_6_eq);
  and and_4 (is_xori, comparator_7_eq, comparator_8_eq);
  and and_5 (is_slli, comparator_9_eq, comparator_10_eq, comparator_11_eq);
  and and_6 (is_srli, comparator_12_eq, comparator_13_eq, comparator_14_eq);
  and and_7 (is_srai, comparator_15_eq, comparator_16_eq, comparator_17_eq);
  and and_8 (is_slti, comparator_18_eq, comparator_19_eq);
  and and_9 (is_add, comparator_20_eq, comparator_21_eq, comparator_22_eq);
  and and_10 (is_sub, comparator_23_eq, comparator_24_eq, comparator_25_eq);
  and and_11 (is_and, comparator_26_eq, comparator_27_eq, comparator_28_eq);
  and and_12 (is_or, comparator_29_eq, comparator_30_eq, comparator_31_eq);
  and and_13 (is_xor, comparator_32_eq, comparator_33_eq, comparator_34_eq);
  and and_14 (is_sll, comparator_35_eq, comparator_36_eq, comparator_37_eq);
  and and_15 (is_srl, comparator_38_eq, comparator_39_eq, comparator_40_eq);
  and and_16 (is_sra, comparator_41_eq, comparator_42_eq, comparator_43_eq);
  and and_17 (is_slt, comparator_44_eq, comparator_45_eq, comparator_46_eq);
  and and_18 (is_mul, comparator_47_eq, comparator_48_eq, comparator_49_eq);
  and and_19 (is_mulh, comparator_47_eq, comparator_50_eq, comparator_49_eq);
  and and_20 (is_mulhu, comparator_47_eq, comparator_51_eq, comparator_49_eq);
  and and_21 (is_beq, comparator_52_eq, comparator_53_eq);
  and and_22 (is_bge, comparator_52_eq, comparator_54_eq);
  and and_23 (is_bgeu, comparator_52_eq, comparator_55_eq);
  and and_24 (is_blt, comparator_52_eq, comparator_56_eq);
  and and_25 (is_bltu, comparator_52_eq, comparator_57_eq);
  and and_26 (is_bne, comparator_52_eq, comparator_58_eq);
  and and_27 (is_lb, comparator_59_eq, comparator_60_eq);
  and and_28 (is_lh, comparator_59_eq, comparator_61_eq);
  and and_29 (is_lw, comparator_59_eq, comparator_62_eq);
  and and_30 (is_sb, comparator_63_eq, comparator_64_eq);
  and and_31 (is_sh, comparator_63_eq, comparator_65_eq);
  and and_32 (is_sw, comparator_63_eq, comparator_66_eq);
  ROM #(.addrWidth(6), .dataWidth(16)) rom_1 (
    .addr(input_ROM), .data({rom_1_data, WBSel, MemRW, ALUSel, BSel, ASel, BrUn, ImmSel, RegWEn}));
  Priority_Encoder #(.select_enc(6)) priority_encoder_1 (
    .in1(is_addi), .in2(is_andi), .in3(is_ori), .in4(is_xori), .in5(is_slli), .in6(is_srli), .in7(is_srai),
    .in8(is_slti), .in9(is_add), .in10(is_sub), .in11(is_and), .in12(is_or), .in13(is_xor), .in14(is_sll),
    .in15(is_srl), .in16(is_sra), .in17(is_slt), .in18(is_mul), .in19(is_mulh), .in20(is_mulhu),
    .in21(is_beq), .in22(is_bge), .in23(is_bgeu), .in24(is_blt), .in25(is_bltu), .in26(is_bne), .in27(is_lb),
    .in28(is_lh), .in29(is_lw), .in30(is_sb), .in31(is_sh), .in32(is_sw), .out(input_ROM));  // open: in0, in33, in34, in35, in36, in37, in38, in39, in40, in41, in42, in43, in44, in45, in46, in47, in48, in49, in50, in51, in52, in53, in54, in55, in56, in57, in58, in59, in60, in61, in62, in63, gs, en_out, en_in
  Comparator #(.width(5)) comparator_67 (.a(Instruction[6:2]), .b(5'b11000), .eq(comparator_67_eq));  // open: gt, lt
  Comparator #(.width(3)) comparator_68 (.a(Instruction[14:12]), .b(3'b000), .eq(comparator_68_eq));  // open: gt, lt
  Comparator #(.width(3)) comparator_69 (.a(Instruction[14:12]), .b(3'b001), .eq(comparator_69_eq));  // open: gt, lt
  not not_1 (not_1_out, BrEq);
  Comparator #(.width(3)) comparator_70 (.a(Instruction[14:12]), .b(3'b100), .eq(comparator_70_eq));  // open: gt, lt
  Comparator #(.width(3)) comparator_71 (.a(Instruction[14:12]), .b(3'b110), .eq(comparator_71_eq));  // open: gt, lt
  Comparator #(.width(3)) comparator_72 (.a(Instruction[14:12]), .b(3'b101), .eq(comparator_72_eq));  // open: gt, lt
  not not_2 (not_2_out, BrLt);
  Comparator #(.width(3)) comparator_73 (.a(Instruction[14:12]), .b(3'b111), .eq(comparator_73_eq));  // open: gt, lt
  not not_3 (not_3_out, BrLt);
  Comparator #(.width(5)) comparator_74 (.a(Instruction[6:2]), .b(5'b11011), .eq(comparator_74_eq));  // open: gt, lt
  Comparator #(.width(5)) comparator_75 (.a(Instruction[6:2]), .b(5'b11001), .eq(comparator_75_eq));  // open: gt, lt
  Comparator #(.width(3)) comparator_76 (.a(Instruction[14:12]), .b(3'b000), .eq(comparator_76_eq));  // open: gt, lt
  and and_33 (and_33_out, comparator_75_eq, comparator_76_eq);
  // Probe on input_ROM
  and and_34 (and_34_out, comparator_67_eq, comparator_68_eq, BrEq);
  and and_35 (and_35_out, comparator_67_eq, comparator_69_eq, not_1_out);
  and and_36 (and_36_out, comparator_67_eq, comparator_70_eq, BrLt);
  and and_37 (and_37_out, comparator_67_eq, comparator_71_eq, BrLt);
  and and_38 (and_38_out, comparator_67_eq, comparator_72_eq, not_2_out);
  and and_39 (and_39_out, comparator_67_eq, comparator_73_eq, not_3_out);
  or or_1 (or_1_out, comparator_74_eq, and_33_out);
  or or_2 (or_2_out, and_34_out, and_35_out, and_36_out, and_37_out, and_38_out, and_39_out);
  or or_3 (PCSel, or_2_out, or_1_out);

  // Other names for the same wires on the sheet: opcode[4:0] = Instruction[6:2]; funct3[2:0] = Instruction[14:12];
  //   funct7_least = Instruction[25]; funct7 = Instruction[30]

  // Notes on the sheet:
  //   INPUTS to your circuit
  //   Connect ROM Input here ->
  //   contents of rom_1 (hex, n*v repeats v):
  //   0 1041 13c1 1341 1241 10c1 12c1 16c1 1141 1001 1601 1381 1301 1201 1081 1281 1681 1101 1401 1481
  //   1581 64 64 74 64 74 64 41 41 41 842 842 842
  //   ROM FOR CONTROL LOGIC
  //   DON'T CHANGE THE LOCATIONS OF THE INPUTS AND OUTPUTS!
  //   This is only if you choose to do the ROM option
  //   CONNECT
  //   WIRE
  //   TO
  //   USE
  //   ROM
  //   OUTPUT from your circuit
  //   Reminder: If using ROM, use combinational logic for PCSel
endmodule
