// Logisim project cpu.circ as structural Verilog: 1 circuit, main circuit cpu
module cpu (
  input  clk,
  input  [31:0] Instruction,
  input  [31:0] MemReadData,
  output [31:0] MemAddress,
  output [31:0] ProgramCounter,
  output [31:0] ra,
  output [31:0] sp,
  output [31:0] t0,
  output [31:0] t1,
  output [31:0] t2,
  output [31:0] s0,
  output [31:0] s1,
  output [31:0] a0,
  output [3:0] MemWriteMask,
  output [31:0] MemWriteData
);

  wire ASel, BrEq, BrLt, BrUn, BSel, MemRW, PCSel, RegWEn;
  wire [1:0] WBSel;
  wire [2:0] input_immsel;
  wire [3:0] input_alusel;
  wire [31:0] input_A, input_B, input_PC, next_PC, output_alu, output_DMem, output_imm, output_rd1,
       output_rd2, output_WB;

  Adder #(.width(32)) adder_1 (.a(ProgramCounter), .b(32'h4), .out(next_PC));  // open: cin, cout
  // Probe on Instruction
  // Probe on Instruction[11:7]
  // Probe on Instruction[19:15]
  // Probe on output_alu
  // Probe on RegWEn
  // Probe on input_immsel
  // Probe on input_alusel
  Multiplexer #(.width(32)) multiplexer_1 (.in0(next_PC), .in1(output_alu), .out(input_PC), .sel(PCSel));
  control_logic control_logic_1 (
    .Instruction(Instruction), .BrEq(BrEq), .BrLt(BrLt), .PCSel(PCSel), .RegWEn(RegWEn),
    .ImmSel(input_immsel), .BrUn(BrUn), .ASel(ASel), .BSel(BSel), .ALUSel(input_alusel), .MemRW(MemRW),
    .WBSel(WBSel));
  Register #(.width(32)) PC (.D(input_PC), .clk(clk), .Q(ProgramCounter));  // open: en, clr
  imm_gen imm_gen_1 (.Instruction(Instruction), .ImmSel(input_immsel), .Immediate(output_imm));
  regfile regfile_1 (
    .rs1(Instruction[19:15]), .rs2(Instruction[24:20]), .rd(Instruction[11:7]), .Write_Data(output_WB),
    .RegWEn(RegWEn), .clk(clk), .ra(ra), .sp(sp), .t0(t0), .t1(t1), .t2(t2), .s0(s0), .s1(s1), .a0(a0),
    .Read_Data_1(output_rd1), .Read_Data_2(output_rd2));
  Multiplexer #(.width(32)) multiplexer_2 (.in0(output_rd1), .in1(ProgramCounter), .out(input_A), .sel(ASel));
  branch_comp branch_comp_1 (.BrData1(output_rd1), .BrData2(output_rd2), .BrUn(BrUn), .BrEq(BrEq), .BrLt(BrLt));
  alu alu_1 (.A(input_A), .B(input_B), .ALUSel(input_alusel), .ALUResult(output_alu));
  Multiplexer #(.width(32)) multiplexer_3 (.in0(output_rd2), .in1(output_imm), .out(input_B), .sel(BSel));
  partial_store partial_store_1 (
    .Instruction(Instruction), .MemAddress(output_alu), .DataFromReg(output_rd2), .MemRW(MemRW),
    .MemWriteMask(MemWriteMask), .DataToMem(MemWriteData));
  Multiplexer #(.select(2), .width(32)) multiplexer_4 (
    .in0(output_DMem), .in1(output_alu), .in2(next_PC), .out(output_WB), .sel(WBSel));  // open: in3
  partial_load partial_load_1 (
    .Instruction(Instruction), .MemAddress(output_alu), .DataFromMem(MemReadData), .DataToReg(output_DMem));

  // Other names for the same wires on the sheet: input_rd[4:0] = Instruction[11:7];
  //   input_rs1[4:0] = Instruction[19:15]; input_rs2[4:0] = Instruction[24:20]

  // Notes on the sheet:
  //   To IMEM
  //   IMEM (do **NOT** move this)
  //   From IMEM
  //   Inputs/Outputs for testing. Do **NOT** move these.
  //   It is OK to move the PC, RegFile, ALU, MEM, Branch Comp, Imm Gen, Partial Load, Partial Store and Control Logic to wherever is most convenient for you when constructing your CPU, and to delete this text
  //   To DMEM
  //   DMEM (do **NOT** move this)
  //   From DMEM
endmodule
